# Fritzing sketch Estufa Futuragora (saved by Fritzing 0.7.12b)
breadboards: 1

parts:
  Arduino1 = Arduino
  J1 = Basic Servo  # not connected
  R1 = Photocell (LDR) [package=THT]
  S1 = Toggle Switch [package=THT]  # not connected
  R2 = Resistor [tolerance=±5% resistance=220 package=THT]
  T1 = LM35 Temperature Sensor [package="TO92 [THT]"]
  T2 = LM35 Temperature Sensor [package="TO92 [THT]"]
  J2 = Infrared Proximity Sensor  # not connected
  K1 = Relay [part_number=FRS1B-S package=THT]
  DIP-Relay1 = DIP-Relay-D31A [part_number=D31A*]
  DIP-Relay2 = DIP-Relay-D31A [part_number=D31A*]
  Part1 = Humidity Sensor - HIH-4030 Breakout
  LED1 = RGB LED (com. anode, rbg) [package="5 mm [THT]"]  # not connected
  Part2 = Humidity Sensor - HIH-4030 Breakout

nets:
  N1: Arduino1.D7, Part2.OUT
  N2: Arduino1.D6, Part1.OUT
  N3: Arduino1.D5, K1.A
  N4: Arduino1.D4, DIP-Relay1.n.c.
  N5: Arduino1.D3, DIP-Relay2.n.c.
  N6: Arduino1.D2, T1.Vout
  N7: Arduino1.D1TX, T2.Vout
  N8: Arduino1.D0RX, R2.Pin_1
  GND: R1.pin_0, T1.GND, T2.GND, K1.COIL1, DIP-Relay1.A2_Switch_Terminal_A, DIP-Relay2.A2_Switch_Terminal_A, Part1.GND, Part2.GND
  N9: R1.pin_1, R2.Pin_0
  VCC: T1.+Vs, T2.+Vs, K1.C1, K1.C2, DIP-Relay1.A1_Switch_Terminal_A, DIP-Relay2.A1_Switch_Terminal_A, Part1.VCC, Part2.VCC
